# Fritzing sketch IOTSEIS785 (saved by Fritzing 0.9.2b)
breadboards: 1

parts:
  Part1 = Photon
  PART1 = Sound Detector
  LED1 = RGB LED - (4 legs) [package="5 mm [THT]"]
  R1 = Resistor [tolerance=±5% resistance=330 package="2512 [SMD]"]
  R2 = Resistor [tolerance=±5% resistance=330 package="2010 [SMD]"]
  R3 = Resistor [tolerance=±5% resistance=330 package="2010 [SMD]"]
  LED2 = smd LED [color="Red (633nm)" package="0603 [SMD]"]
  R4 = Resistor [tolerance=±5% resistance=330 package="2010 [SMD]"]

nets:
  N1: Part1.A0, PART1.ENVELOPE
  N2: Part1.RX, PART1.AUDIO
  GND: Part1.GND, PART1.GND, LED1.red_cathode, LED2.cathode
  N3: Part1.D0, LED1.common_anode, R3.Pin_0, R3.Pin_1
  N4: Part1.D1, LED1.green_cathode, R2.Pin_0, R2.Pin_1
  N5: Part1.D2, LED1.blue_cathode, R1.Pin_0, R1.Pin_1
  N6: Part1.D3, PART1.GATE
  N7: Part1.D7, LED2.anode, R4.Pin_0, R4.Pin_1
  3V3: Part1.3V3, PART1.VCC

custom parts:
  Sound Detector: Electret microphone with multiple outputs. - First output is the actual audio - Second output is the amplitude envelope - Third output is a binary "sound present" indication - high while sound is present, low otherwise. Visit sparkfun.com for more documentations.
